// Logisim project Domaci_zadatak_2.circ as structural Verilog: 2 circuits, main circuit min
module min (
  input  x1,
  input  x2,
  input  x3,
  input  x4,
  input  x5,
  output y
);

  wire and_1_out, and_2_out, and_4_out, not_1_out, not_2_out;

  not not_1 (not_1_out, x1);
  and and_1 (and_1_out, not_1_out, x2);
  not not_2 (not_2_out, x3);
  and and_2 (and_2_out, and_1_out, not_2_out);
  and and_3 (y, and_2_out, and_4_out);
  and and_4 (and_4_out, x4, x5);

  // Notes on the sheet:
  //   7+4=11     11>01011
endmodule

module NILI_log_kola (
  input  in_1,
  input  in_2,
  input  in_3,
  input  in_4,
  input  in_5,
  output out_6
);

  wire nor_1_out, nor_2_out, nor_3_out, nor_4_out, nor_5_out, nor_6_out, nor_7_out, nor_8_out, nor_9_out;

  nor nor_1 (nor_1_out, in_2, in_2);
  nor nor_2 (nor_2_out, in_4, in_4);
  nor nor_3 (nor_3_out, in_5, in_5);
  nor nor_4 (nor_4_out, nor_2_out, nor_3_out);
  nor nor_5 (nor_5_out, in_1, nor_1_out);
  nor nor_6 (nor_6_out, nor_5_out, nor_5_out);
  nor nor_7 (nor_7_out, nor_6_out, in_3);
  nor nor_8 (nor_8_out, nor_4_out, nor_4_out);
  nor nor_9 (nor_9_out, nor_7_out, nor_7_out);
  nor nor_10 (out_6, nor_9_out, nor_8_out);
endmodule
